// Logisim project ctrl_sub.circ as structural Verilog: 3 circuits, main circuit main
module CONTROL (
  output FETA,
  output RDA,
  output FETB,
  output RDB,
  output SUBST,
  output FETC,
  output BR,
  output CLK,
  output RESET
);

  wire d_ff_8_q, not_1_out;

  D_Flip_Flop d_ff_1 (.D(d_ff_8_q), .clk(CLK), .Q(FETA), .preset(not_1_out));  // open: Qn, reset
  not not_1 (not_1_out, RESET);
  D_Flip_Flop d_ff_2 (.D(FETA), .clk(CLK), .Q(RDA), .reset(not_1_out));  // open: Qn, preset
  D_Flip_Flop d_ff_3 (.D(RDA), .clk(CLK), .Q(FETB), .reset(not_1_out));  // open: Qn, preset
  D_Flip_Flop d_ff_4 (.D(FETB), .clk(CLK), .Q(RDB), .reset(not_1_out));  // open: Qn, preset
  D_Flip_Flop d_ff_5 (.D(RDB), .clk(CLK), .Q(SUBST), .reset(not_1_out));  // open: Qn, preset
  D_Flip_Flop d_ff_6 (.D(SUBST), .clk(CLK), .Q(FETC), .reset(not_1_out));  // open: Qn, preset
  D_Flip_Flop d_ff_7 (.D(FETC), .clk(CLK), .Q(BR), .reset(not_1_out));  // open: Qn, preset
  D_Flip_Flop d_ff_8 (.D(BR), .clk(CLK), .Q(d_ff_8_q), .reset(not_1_out));  // open: Qn, preset
endmodule

module main (
);

  wire A_ld, and_2_out, and_3_out, branch, clk, d_ff_1_qn, d_ff_2_qn, d_ff_3_qn, leq, MAR_ld, MAR_src, PC_we,
       RAM_we, res, S0, S1, S3, S4, S6, S7, subtractor_1_bout;
  wire [2:0] d_ff_1_q;
  wire [7:0] A_val, adder_1_out, addr, alu_out, and_1_out, data, idk, multiplexer_1_out, multiplexer_2_out,
       nor_1_out, ram_out;

  Adder adder_1 (.a(8'h1), .b(addr), .out(adder_1_out));  // open: cin, cout
  Multiplexer #(.width(8)) multiplexer_1 (.in0(adder_1_out), .in1(ram_out), .out(multiplexer_1_out), .sel(branch));
  assign and_1_out = {8{1'b1}} & idk;  // AND_Gate and_1, 8 bits wide
  Register pc (.D(multiplexer_1_out), .en(PC_we), .clk(clk), .Q(addr), .clr(res));
  and and_2 (and_2_out, and_1_out[0], and_1_out[1], and_1_out[2], and_1_out[3], and_1_out[4], and_1_out[5], and_1_out[6], and_1_out[7]);
  // Probe on A_val
  Multiplexer #(.width(8)) multiplexer_2 (.in0({8{1'b1}}), .in1(A_val), .out(multiplexer_2_out), .sel(and_2_out));
  Decoder #(.enable("false"), .select(3)) decoder_1 (
    .out0(S0), .out1(S1), .out2(A_ld), .out3(S3), .out4(S4), .out5(RAM_we), .out6(S6), .out7(S7),
    .sel(d_ff_1_q));
  D_Flip_Flop d_ff_1 (.D(d_ff_1_qn), .clk(clk), .Q(d_ff_1_q[0]), .Qn(d_ff_1_qn), .reset(res));  // open: preset
  RAM ram_1 (.addr(addr), .we(RAM_we), .oe(1'b1), .clk(clk), .din(alu_out), .dout(ram_out));
  TTY tty_1 (.data(multiplexer_2_out[6:0]), .clk(clk), .we(and_2_out), .clr(res));
  D_Flip_Flop d_ff_2 (.D(d_ff_2_qn), .clk(d_ff_1_qn), .Q(d_ff_1_q[1]), .Qn(d_ff_2_qn), .reset(res));  // open: preset
  D_Flip_Flop d_ff_3 (.D(d_ff_3_qn), .clk(d_ff_2_qn), .Q(d_ff_1_q[2]), .Qn(d_ff_3_qn), .reset(res));  // open: preset
  Register A (.D(data), .en(A_ld), .clk(clk), .Q(A_val), .clr(res));
  Clock clock_1 (.out(clk));
  Button button_1 (.out(res));
  Subtractor subtractor_1 (.a(data), .b(A_val), .out(alu_out), .bout(subtractor_1_bout));  // open: bin
  Multiplexer #(.width(8)) multiplexer_3 (.in0(addr), .in1(ram_out), .out(idk), .sel(MAR_src));
  // Probe on alu_out
  Register MAR (.D(idk), .en(MAR_ld), .clk(clk), .Q(data), .clr(res));
  assign nor_1_out = ~(alu_out | {8{1'b0}});  // NOR_Gate nor_1, 8 bits wide
  or or_1 (PC_we, A_ld, RAM_we, S7);
  and and_3 (and_3_out, nor_1_out[0], nor_1_out[1], nor_1_out[2], nor_1_out[3], nor_1_out[4], nor_1_out[5], nor_1_out[6], nor_1_out[7]);
  or or_2 (MAR_ld, S0, S1, S6, S3, S4);
  or or_3 (MAR_src, S1, S6, S4);
  and and_4 (branch, leq, S7);
  or or_4 (leq, and_3_out, subtractor_1_bout);

  // Other names for the same wires on the sheet: S2 = A_ld; S5 = RAM_we; should_branch = S7
endmodule

module incrementer (
  input  [7:0] A,
  output [7:0] sum
);

  Adder adder_1 (.a(8'h1), .b(A), .out(sum));  // open: cin, cout
endmodule
